// Logisim project Guia_0507.circ as structural Verilog: 2 circuits, main circuit main
module main (
  input  a,
  input  b,
  output out_3
);

  wire nor_1_out, nor_2_out;

  nor nor_1 (nor_1_out, a, a);
  \xor  Custom_Xor (.s(out_3), .a(nor_1_out), .b(nor_2_out));
  nor nor_2 (nor_2_out, b, b);
endmodule

module \xor  (
  input  a,
  input  b,
  output s
);

  wire xor_1_out, xor_2_out, xor_3_out, xor_4_out;

  xor xor_1 (xor_1_out, a, a);
  xor xor_2 (xor_2_out, a, xor_1_out);
  xor xor_3 (xor_3_out, xor_1_out, a);
  xor xor_4 (xor_4_out, xor_2_out, xor_3_out);
  xor xor_5 (s, xor_4_out, xor_4_out);
endmodule
