// Logisim project R0203.circ as structural Verilog: 1 circuit, main circuit main
module main (
  input  in_1,
  output out_2,
  output out_3,
  output out_4
);

  wire clock_1_out, j_k_ff_1_qn, j_k_ff_2_qn;

  Clock clock_1 (.out(clock_1_out));
  J_K_Flip_Flop j_k_ff_1 (.J(in_1), .clk(clock_1_out), .K(in_1), .Q(out_2), .Qn(j_k_ff_1_qn));  // open: preset, reset
  J_K_Flip_Flop j_k_ff_2 (
    .J(j_k_ff_1_qn), .clk(clock_1_out), .K(j_k_ff_1_qn), .Q(out_3), .Qn(j_k_ff_2_qn));  // open: preset, reset
  J_K_Flip_Flop j_k_ff_3 (.J(j_k_ff_2_qn), .clk(clock_1_out), .K(j_k_ff_2_qn), .Q(out_4));  // open: Qn, preset, reset
endmodule
