// Logisim project R0205.circ as structural Verilog: 1 circuit, main circuit main
module main (
  input  in_1,
  input  in_2,
  output F0,
  output out_4,
  output out_5,
  output out_6
);

  wire and_1_out, and_2_out, clock_1_out;

  Clock clock_1 (.out(clock_1_out));
  T_Flip_Flop t_ff_1 (.clk(clock_1_out), .T(in_1), .Q(F0), .reset(in_2));  // open: Qn, preset
  T_Flip_Flop t_ff_2 (.clk(F0), .T(F0), .Q(out_4), .reset(in_2));  // open: Qn, preset
  and and_1 (and_1_out, F0, out_4);
  and and_2 (and_2_out, out_4, out_5);
  T_Flip_Flop t_ff_3 (.clk(out_4), .T(and_1_out), .Q(out_5), .reset(in_2));  // open: Qn, preset
  T_Flip_Flop t_ff_4 (.clk(out_5), .T(and_2_out), .Q(out_6), .reset(in_2));  // open: Qn, preset

  // Notes on the sheet:
  //   F1
  //   F2
  //   F3
endmodule
