// Logisim project PA0204C.circ as structural Verilog: 1 circuit, main circuit main
module main (
  input  A,
  input  B,
  input  C,
  input  in_4,
  input  in_5,
  output OUT
);

  wire and_1_out, and_2_out, clock_1_out, or_1_out;

  or or_1 (or_1_out, B, and_1_out);
  and and_1 (and_1_out, A, C);
  and and_2 (and_2_out, A, C);
  Clock clock_1 (.out(clock_1_out));
  S_R_Flip_Flop s_r_ff_1 (
    .S(and_2_out), .clk(clock_1_out), .R(or_1_out), .Q(OUT), .preset(in_4), .reset(in_5));  // open: Qn
endmodule
