// Logisim project Circuitos.circ as structural Verilog: 6 circuits, main circuit ULA-1bit
// Full_Adder
module FULL_ADDER (
  input  a,
  input  CarryIn,
  input  b,
  output Sum,
  output Overflow
);

  wire and_1_out, and_2_out, xor_1_out;

  xor xor_1 (xor_1_out, a, b);
  and and_1 (and_1_out, a, b);
  xor xor_2 (Sum, xor_1_out, CarryIn);
  and and_2 (and_2_out, CarryIn, xor_1_out);
  or or_1 (Overflow, and_2_out, and_1_out);
endmodule

// MUX_2x1
module MUX_2x1 (
  input  Op,
  input  A,
  input  B,
  output out_4
);

  wire and_1_out, and_2_out, not_1_out;

  not not_1 (not_1_out, Op);
  and and_1 (and_1_out, A, not_1_out);
  and and_2 (and_2_out, B, Op);
  or or_1 (out_4, and_1_out, and_2_out);

  // Notes on the sheet:
  //   806454 - Yago Almeida
endmodule

// MUX_4x2
module MUX_4x2 (
  input  Op1,
  input  Op0,
  input  A,
  input  B,
  input  C,
  input  D,
  output S
);

  wire and_1_out, and_2_out, and_3_out, and_4_out, not_1_out, not_2_out;

  not not_1 (not_1_out, Op1);
  not not_2 (not_2_out, Op0);
  and and_1 (and_1_out, A, not_1_out, not_2_out);
  and and_2 (and_2_out, B, not_1_out, Op0);
  or or_1 (S, and_1_out, and_2_out, and_3_out, and_4_out);
  and and_3 (and_3_out, C, Op1, not_2_out);
  and and_4 (and_4_out, D, Op1, Op0);
endmodule

module ULA_1bit (
  input  CarryIn,
  input  Op1,
  input  Op0,
  input  BInvert,
  input  A,
  input  B,
  output Result,
  output CarryOut
);

  wire and_1_out, full_adder_1_sum, mux_2x1_1_out_4, not_1_out, not_2_out, or_1_out;

  not not_1 (not_1_out, B);
  MUX_2x1 mux_2x1_1 (.A(B), .B(not_1_out), .Op(BInvert), .out_4(mux_2x1_1_out_4));
  and and_1 (and_1_out, A, mux_2x1_1_out_4);
  or or_1 (or_1_out, A, mux_2x1_1_out_4);
  not not_2 (not_2_out, A);
  FULL_ADDER full_adder_1 (.a(A), .b(mux_2x1_1_out_4), .CarryIn(CarryIn), .Sum(full_adder_1_sum), .Overflow(CarryOut));
  MUX_4x2 mux_4x2_1 (
    .A(and_1_out), .B(or_1_out), .C(not_2_out), .D(full_adder_1_sum), .Op1(Op1), .Op0(Op0), .S(Result));

  // Notes on the sheet:
  //   806454 - Yago Almeida
endmodule

module ULA_4bits (
  input  BInvert,
  input  OP1,
  input  OP0,
  input  B3,
  input  B2,
  input  B1,
  input  B0,
  input  A3,
  input  A2,
  input  A1,
  input  A0,
  output S0,
  output S1,
  output S2,
  output S3,
  output Cout
);

  wire ula_1bit_1_carryout, ula_1bit_2_carryout, ula_1bit_3_carryout;

  ULA_1bit ula_1bit_1 (
    .A(A0), .B(B0), .BInvert(BInvert), .CarryIn(BInvert), .Op1(OP1), .Op0(OP0),
    .CarryOut(ula_1bit_1_carryout), .Result(S0));
  ULA_1bit ula_1bit_2 (
    .A(A1), .B(B1), .BInvert(BInvert), .CarryIn(ula_1bit_1_carryout), .Op1(OP1), .Op0(OP0),
    .CarryOut(ula_1bit_2_carryout), .Result(S1));
  ULA_1bit ula_1bit_3 (
    .A(A2), .B(B2), .BInvert(BInvert), .CarryIn(ula_1bit_2_carryout), .Op1(OP1), .Op0(OP0),
    .CarryOut(ula_1bit_3_carryout), .Result(S2));
  ULA_1bit ula_1bit_4 (
    .A(A3), .B(B3), .BInvert(BInvert), .CarryIn(ula_1bit_3_carryout), .Op1(OP1), .Op0(OP0), .CarryOut(Cout),
    .Result(S3));

  // Notes on the sheet:
  //   806454 -Yago Almeida
  //   OP 00 = AND
  //   OP 01 = OR
  //   OP 10 = NOT(A)
  //   OP 11 = SUM
endmodule

module ULA_74LS181 (
  input  [3:0] A,
  input  [3:0] B,
  input  [3:0] OP,
  output [3:0] S
);

  wire [3:0] and_1_out, and_2_out, and_3_out, nand_1_out, nor_1_out, not_1_out, not_2_out, or_1_out,
       or_2_out, or_3_out, xnor_1_out, xor_1_out;

  assign not_1_out = ~A;  // NOT_Gate not_1, 4 bits wide
  assign not_2_out = ~B;  // NOT_Gate not_2, 4 bits wide
  assign and_1_out = A & B;  // AND_Gate and_1, 4 bits wide
  assign nor_1_out = ~(A | B);  // NOR_Gate nor_1, 4 bits wide
  assign and_2_out = ~A & B;  // AND_Gate and_2, 4 bits wide
  assign nand_1_out = ~(A & B);  // NAND_Gate nand_1, 4 bits wide
  assign xor_1_out = A ^ B;  // XOR_Gate xor_1, 4 bits wide
  assign and_3_out = A & ~B;  // AND_Gate and_3, 4 bits wide
  assign or_1_out = ~A | B;  // OR_Gate or_1, 4 bits wide
  assign xnor_1_out = ~(A ^ B);  // XNOR_Gate xnor_1, 4 bits wide
  assign or_2_out = A | ~B;  // OR_Gate or_2, 4 bits wide
  assign or_3_out = A | B;  // OR_Gate or_3, 4 bits wide
  Multiplexer #(.select(4), .width(4), .enable("false")) multiplexer_1 (
    .in0(not_1_out), .in1(nor_1_out), .in2(and_2_out), .in3(4'b0000), .in4(nand_1_out), .in5(not_2_out),
    .in6(xor_1_out), .in7(and_3_out), .in8(or_1_out), .in9(xnor_1_out), .in10(B), .in11(and_1_out),
    .in12(4'b1111), .in13(or_2_out), .in14(or_3_out), .in15(B), .out(S), .sel(OP));

  // Notes on the sheet:
  //   806454 - Yago Almeida
endmodule
